# Fritzing sketch MQTT_Two_button (saved by Fritzing 0.9.2b)
circuit board: 8.46667cm x 5.64444cm
breadboards: 1

parts:
  Part2 = Arduino Ethernet Shield (Rev3)
  S1 = Pushbutton [package="[THT]"]
  S2 = Pushbutton [package="[THT]"]
  R1 = Resistor [tolerance=±5% resistance=220 package="2010 [SMD]"]
  R2 = Resistor [tolerance=±5% resistance=220 package="2010 [SMD]"]
  LED1 = LED - 5mm [color="Red (633nm)" package="5 mm [THT]"]
  R3 = Resistor [tolerance=±5% resistance=220 package="2010 [SMD]"]

nets:
  N1: Part2.5V, R1.Pin_0, R2.Pin_0
  N2: Part2.GND, S1.Pin_1, S1.Pin_2, S2.Pin_1, S2.Pin_2, R3.Pin_0
  N3: Part2.D8, S2.Pin_3, S2.Pin_4, R2.Pin_1
  N4: Part2.PWM_D9, LED1.anode
  N5: Part2.D7, S1.Pin_3, S1.Pin_4, R1.Pin_1
  N6: LED1.cathode, R3.Pin_1
